// Logisim project processor.circ as structural Verilog
module RegisterFile (
  input  [31:0] rd_data_in,
  input  [4:0] rs1_addr,
  input  [4:0] rs2_addr,
  input  [4:0] rd_addr,
  input  reg_write_en,
  output [31:0] rs1_data,
  output [31:0] rs2_data
);

  wire clk, w0, w1, w2, w3, w4, w5, w6, w7, w8, w9, w10, w11, w12, w13, w14, w15, w16, w17, w18, w19, w20,
       w21, w22, w23, w24, w25, w26, w27, w28, w29, w30, w31;
  wire [31:0] q0, q1, q2, q3, q4, q5, q6, q7, q8, q9, q10, q11, q12, q13, q14, q15, q16, q17, q18, q19, q20,
       q21, q22, q23, q24, q25, q26, q27, q28, q29, q30, q31;

  Clock u_clk (.out(clk));
  Multiplexer #(.select(5), .width(32)) multiplexer_1 (
    .in0(q0), .in1(q1), .in2(q2), .in3(q3), .in4(q4), .in5(q5), .in6(q6), .in7(q7), .in8(q8), .in9(q9),
    .in10(q10), .in11(q11), .in12(q12), .in13(q13), .in14(q14), .in15(q15), .in16(q16), .in17(q17),
    .in18(q18), .in19(q19), .in20(q20), .in21(q21), .in22(q22), .in23(q23), .in24(q24), .in25(q25),
    .in26(q26), .in27(q27), .in28(q28), .in29(q29), .in30(q30), .in31(q31), .out(rs1_data), .sel(rs1_addr));
  Demultiplexer #(.select(5)) demultiplexer_1 (
    .out0(w0), .out1(w1), .out2(w2), .out3(w3), .out4(w4), .out5(w5), .out6(w6), .out7(w7), .out8(w8),
    .out9(w9), .out10(w10), .out11(w11), .out12(w12), .out13(w13), .out14(w14), .out15(w15), .out16(w16),
    .out17(w17), .out18(w18), .out19(w19), .out20(w20), .out21(w21), .out22(w22), .out23(w23), .out24(w24),
    .out25(w25), .out26(w26), .out27(w27), .out28(w28), .out29(w29), .out30(w30), .out31(w31),
    .in(reg_write_en), .sel(rd_addr));
  Multiplexer #(.select(5), .width(32)) multiplexer_2 (
    .in0(q0), .in1(q1), .in2(q2), .in3(q3), .in4(q4), .in5(q5), .in6(q6), .in7(q7), .in8(q8), .in9(q9),
    .in10(q10), .in11(q11), .in12(q12), .in13(q13), .in14(q14), .in15(q15), .in16(q16), .in17(q17),
    .in18(q18), .in19(q19), .in20(q20), .in21(q21), .in22(q22), .in23(q23), .in24(q24), .in25(q25),
    .in26(q26), .in27(q27), .in28(q28), .in29(q29), .in30(q30), .in31(q31), .out(rs2_data), .sel(rs2_addr));
  Register #(.width(32)) register_1 (.D({32{1'b0}}), .en(w0), .clk(clk), .Q(q0));  // open: clr
  Register #(.width(32)) register_2 (.D(rd_data_in), .en(w4), .clk(clk), .Q(q4));  // open: clr
  Register #(.width(32)) register_3 (.D(rd_data_in), .en(w8), .clk(clk), .Q(q8));  // open: clr
  Register #(.width(32)) register_4 (.D(rd_data_in), .en(w12), .clk(clk), .Q(q12));  // open: clr
  Register #(.width(32)) register_5 (.D(rd_data_in), .en(w16), .clk(clk), .Q(q16));  // open: clr
  Register #(.width(32)) register_6 (.D(rd_data_in), .en(w20), .clk(clk), .Q(q20));  // open: clr
  Register #(.width(32)) register_7 (.D(rd_data_in), .en(w24), .clk(clk), .Q(q24));  // open: clr
  Register #(.width(32)) register_8 (.D(rd_data_in), .en(w28), .clk(clk), .Q(q28));  // open: clr
  Register #(.width(32)) register_9 (.D(rd_data_in), .en(w1), .clk(clk), .Q(q1));  // open: clr
  Register #(.width(32)) register_10 (.D(rd_data_in), .en(w5), .clk(clk), .Q(q5));  // open: clr
  Register #(.width(32)) register_11 (.D(rd_data_in), .en(w9), .clk(clk), .Q(q9));  // open: clr
  Register #(.width(32)) register_12 (.D(rd_data_in), .en(w13), .clk(clk), .Q(q13));  // open: clr
  Register #(.width(32)) register_13 (.D(rd_data_in), .en(w17), .clk(clk), .Q(q17));  // open: clr
  Register #(.width(32)) register_14 (.D(rd_data_in), .en(w21), .clk(clk), .Q(q21));  // open: clr
  Register #(.width(32)) register_15 (.D(rd_data_in), .en(w25), .clk(clk), .Q(q25));  // open: clr
  Register #(.width(32)) register_16 (.D(rd_data_in), .en(w29), .clk(clk), .Q(q29));  // open: clr
  Register #(.width(32)) register_17 (.D(rd_data_in), .en(w2), .clk(clk), .Q(q2));  // open: clr
  Register #(.width(32)) register_18 (.D(rd_data_in), .en(w6), .clk(clk), .Q(q6));  // open: clr
  Register #(.width(32)) register_19 (.D(rd_data_in), .en(w10), .clk(clk), .Q(q10));  // open: clr
  Register #(.width(32)) register_20 (.D(rd_data_in), .en(w14), .clk(clk), .Q(q14));  // open: clr
  Register #(.width(32)) register_21 (.D(rd_data_in), .en(w18), .clk(clk), .Q(q18));  // open: clr
  Register #(.width(32)) register_22 (.D(rd_data_in), .en(w22), .clk(clk), .Q(q22));  // open: clr
  Register #(.width(32)) register_23 (.D(rd_data_in), .en(w26), .clk(clk), .Q(q26));  // open: clr
  Register #(.width(32)) register_24 (.D(rd_data_in), .en(w30), .clk(clk), .Q(q30));  // open: clr
  Register #(.width(32)) register_25 (.D(rd_data_in), .en(w3), .clk(clk), .Q(q3));  // open: clr
  Register #(.width(32)) register_26 (.D(rd_data_in), .en(w7), .clk(clk), .Q(q7));  // open: clr
  Register #(.width(32)) register_27 (.D(rd_data_in), .en(w11), .clk(clk), .Q(q11));  // open: clr
  Register #(.width(32)) register_28 (.D(rd_data_in), .en(w15), .clk(clk), .Q(q15));  // open: clr
  Register #(.width(32)) register_29 (.D(rd_data_in), .en(w19), .clk(clk), .Q(q19));  // open: clr
  Register #(.width(32)) register_30 (.D(rd_data_in), .en(w23), .clk(clk), .Q(q23));  // open: clr
  Register #(.width(32)) register_31 (.D(rd_data_in), .en(w27), .clk(clk), .Q(q27));  // open: clr
  Register #(.width(32)) register_32 (.D(rd_data_in), .en(w31), .clk(clk), .Q(q31));  // open: clr
endmodule

module ByteAddrMemory (
  input  mem_write_en,
  input  [24:0] addr,
  input  [31:0] write_data,
  input  [1:0] access_size,
  output [31:0] read_data
);

  wire clk, memorylogic_1_byte_0, memorylogic_1_byte_1, memorylogic_1_byte_2, memorylogic_1_byte_3;
  wire [7:0] multiplexer_1_out, ram_1_dout_2, ram_1_dout_3;
  wire [15:0] multiplexer_2_out, ram_1_dout;
  wire [31:0] bit_extender_1_out, bit_extender_2_out;

  Clock u_clk (.out(clk));
  MemoryLogic memorylogic_1 (
    .A(access_size[1]), .B(access_size[0]), .C(addr[1]), .D(addr[0]), .byte_0(memorylogic_1_byte_0),
    .byte_1(memorylogic_1_byte_1), .byte_2(memorylogic_1_byte_2), .byte_3(memorylogic_1_byte_3));
  RAM #(.addrWidth(23), .asyncread("true"), .byteenables("byteEnables"), .dataWidth(32), .\type ("nonvolatile")) ram_1 (
    .addr(addr[24:2]), .we(mem_write_en), .oe(1'b1), .clk(clk), .din(write_data),
    .dout({ram_1_dout, ram_1_dout_3, ram_1_dout_2}), .be3(memorylogic_1_byte_3), .be2(memorylogic_1_byte_2),
    .be1(memorylogic_1_byte_1), .be0(memorylogic_1_byte_0));
  Multiplexer #(.select(2), .width(8)) multiplexer_1 (
    .in0(ram_1_dout_2), .in1(ram_1_dout_3), .in2(ram_1_dout[7:0]), .in3(ram_1_dout[15:8]),
    .out(multiplexer_1_out), .sel(addr[1:0]));
  Multiplexer #(.width(16)) multiplexer_2 (
    .in0(ram_1_dout), .in1({ram_1_dout_3, ram_1_dout_2}), .out(multiplexer_2_out), .sel(addr[1]));
  assign bit_extender_1_out = {{24{multiplexer_1_out[7]}}, multiplexer_1_out};  // Bit_Extender bit_extender_1
  assign bit_extender_2_out = {{16{multiplexer_2_out[15]}}, multiplexer_2_out};  // Bit_Extender bit_extender_2
  Multiplexer #(.select(2), .width(32)) multiplexer_3 (
    .in0(bit_extender_1_out), .in1(bit_extender_2_out), .in2({ram_1_dout, ram_1_dout_3, ram_1_dout_2}),
    .out(read_data), .sel(access_size));  // open: in3

  // Other names for the same wires on the sheet: B = access_size[0]; A = access_size[1]; ADDR_t[1:0] = addr[1:0];
  //   D = addr[0]; C = addr[1]
endmodule

module MemoryLogic (
  input  A,
  input  B,
  input  C,
  input  D,
  output byte_0,
  output byte_1,
  output byte_2,
  output byte_3
);

  wire and_4_out, and_5_out, and_6_out, and_7_out, and_8_out, and_9_out, and_10_out, and_11_out, byte_access,
       half_access, not_1_out, not_2_out, not_3_out, not_4_out, word_access;

  not not_1 (not_1_out, C);
  not not_2 (not_2_out, B);
  not not_3 (not_3_out, A);
  not not_4 (not_4_out, D);
  and and_1 (word_access, A, not_2_out);
  and and_2 (half_access, B, not_3_out);
  and and_3 (byte_access, not_3_out, not_2_out);
  and and_4 (and_4_out, half_access, not_1_out);
  and and_5 (and_5_out, byte_access, not_1_out, not_4_out);
  and and_6 (and_6_out, half_access, not_1_out);
  and and_7 (and_7_out, byte_access, not_1_out, D);
  and and_8 (and_8_out, half_access, C);
  and and_9 (and_9_out, byte_access, C, not_4_out);
  and and_10 (and_10_out, half_access, C);
  and and_11 (and_11_out, byte_access, C, D);
  or or_1 (byte_0, word_access, and_4_out, and_5_out);
  or or_2 (byte_1, word_access, and_6_out, and_7_out);
  or or_3 (byte_2, word_access, and_8_out, and_9_out);
  or or_4 (byte_3, word_access, and_10_out, and_11_out);
endmodule

// SUB
module Compare (
  input  [1:0] SEL,
  input  [31:0] B,
  input  [31:0] A,
  output C_OUT,
  output COMP
);

  wire arithmetic_1_overflow;
  wire [31:0] arithmetic_1_sum;

  Arithmetic arithmetic_1 (
    .ADD_SUB(SEL), .B(B), .A(A), .SUM(arithmetic_1_sum), .Overflow(arithmetic_1_overflow), .C_OUT(C_OUT));
  xor xor_1 (COMP, arithmetic_1_overflow, arithmetic_1_sum[31]);
endmodule

module Logical (
  input  [31:0] A,
  input  [1:0] SEL,
  input  [31:0] B,
  output [31:0] Result
);

  wire [31:0] and_1_out, nor_1_out, or_1_out, xor_1_out;

  assign and_1_out = A & B;  // AND_Gate and_1, 32 bits wide
  assign or_1_out = A | B;  // OR_Gate or_1, 32 bits wide
  assign nor_1_out = ~(A | B);  // NOR_Gate nor_1, 32 bits wide
  assign xor_1_out = A ^ B;  // XOR_Gate xor_1, 32 bits wide
  Multiplexer #(.select(2), .width(32)) multiplexer_1 (
    .in0(and_1_out), .in1(or_1_out), .in2(nor_1_out), .in3(xor_1_out), .out(Result), .sel(SEL));

  // Notes on the sheet:
  //   0    0
  //   0    1
  //   1    0
  //   1    1
  //   SELECTOR TRUTH TABLE
  //   AND
  //   OR
  //   NOR
  //   XOR
endmodule

module Extender (
  input  [31:0] bitsIn,
  input  [1:0] shiftOp,
  output [62:0] extended
);

  wire [30:0] bit_extender_1_out;

  assign bit_extender_1_out = {{30{bitsIn[31]}}, bitsIn[31]};  // Bit_Extender bit_extender_1
  Multiplexer #(.select(2), .width(63)) multiplexer_1 (
    .in0({{31{1'b0}}, bitsIn}), .in1({bit_extender_1_out, bitsIn}), .in2({bitsIn[30:0], bitsIn}),
    .in3({bitsIn, {31{1'b0}}}), .out(extended), .sel(shiftOp));

  // Notes on the sheet:
  //   SRL
  //   SRA
  //   ROR
  //   SLL
endmodule

module halfAdder (
  input  A,
  input  B,
  output S,
  output C
);

  xor xor_1 (S, A, B);
  and and_1 (C, A, B);
endmodule

module fullAdder (
  input  A,
  input  B,
  input  C_IN,
  output Sum,
  output C_OUT
);

  wire halfadder_1_c, halfadder_1_s, halfadder_2_c;

  halfAdder halfadder_1 (.A(A), .B(B), .S(halfadder_1_s), .C(halfadder_1_c));
  halfAdder halfadder_2 (.A(C_IN), .B(halfadder_1_s), .S(Sum), .C(halfadder_2_c));
  or or_1 (C_OUT, halfadder_2_c, halfadder_1_c);
endmodule

module rippleCarry (
  input  A0,
  input  B0,
  input  C_IN,
  input  A1,
  input  B1,
  input  A2,
  input  B2,
  input  A3,
  input  B3,
  input  A4,
  input  B4,
  input  A5,
  input  B5,
  input  A6,
  input  B6,
  input  A7,
  input  B7,
  input  A8,
  input  B8,
  input  A9,
  input  B9,
  input  A10,
  input  B10,
  input  A11,
  input  B11,
  input  A12,
  input  B12,
  input  A13,
  input  B13,
  input  A14,
  input  B14,
  input  A15,
  input  B15,
  input  A16,
  input  B16,
  input  A17,
  input  B17,
  input  A18,
  input  B18,
  input  A19,
  input  B19,
  input  A20,
  input  B20,
  input  A21,
  input  B21,
  input  A22,
  input  B22,
  input  A23,
  input  B23,
  input  A24,
  input  B24,
  input  A25,
  input  B25,
  input  A26,
  input  B26,
  input  A27,
  input  B27,
  input  A28,
  input  B28,
  input  A29,
  input  B29,
  input  A30,
  input  B30,
  input  A31,
  input  B31,
  output [31:0] SUM,
  output Overflow,
  output C_OUT
);

  wire fulladder_1_c_out, fulladder_2_c_out, fulladder_3_c_out, fulladder_4_c_out, fulladder_5_c_out,
       fulladder_6_c_out, fulladder_7_c_out, fulladder_8_c_out, fulladder_9_c_out, fulladder_10_c_out,
       fulladder_11_c_out, fulladder_12_c_out, fulladder_13_c_out, fulladder_14_c_out, fulladder_15_c_out,
       fulladder_16_c_out, fulladder_17_c_out, fulladder_18_c_out, fulladder_19_c_out, fulladder_20_c_out,
       fulladder_21_c_out, fulladder_22_c_out, fulladder_23_c_out, fulladder_24_c_out, fulladder_25_c_out,
       fulladder_26_c_out, fulladder_27_c_out, fulladder_28_c_out, fulladder_29_c_out, fulladder_30_c_out,
       fulladder_31_c_out;

  fullAdder fulladder_1 (.A(A0), .B(B0), .C_IN(C_IN), .Sum(SUM[0]), .C_OUT(fulladder_1_c_out));
  fullAdder fulladder_2 (.A(A1), .B(B1), .C_IN(fulladder_1_c_out), .Sum(SUM[1]), .C_OUT(fulladder_2_c_out));
  fullAdder fulladder_3 (.A(A2), .B(B2), .C_IN(fulladder_2_c_out), .Sum(SUM[2]), .C_OUT(fulladder_3_c_out));
  fullAdder fulladder_4 (.A(A3), .B(B3), .C_IN(fulladder_3_c_out), .Sum(SUM[3]), .C_OUT(fulladder_4_c_out));
  fullAdder fulladder_5 (.A(A4), .B(B4), .C_IN(fulladder_4_c_out), .Sum(SUM[4]), .C_OUT(fulladder_5_c_out));
  fullAdder fulladder_6 (.A(A5), .B(B5), .C_IN(fulladder_5_c_out), .Sum(SUM[5]), .C_OUT(fulladder_6_c_out));
  fullAdder fulladder_7 (.A(A6), .B(B6), .C_IN(fulladder_6_c_out), .Sum(SUM[6]), .C_OUT(fulladder_7_c_out));
  fullAdder fulladder_8 (.A(A7), .B(B7), .C_IN(fulladder_7_c_out), .Sum(SUM[7]), .C_OUT(fulladder_8_c_out));
  fullAdder fulladder_9 (.A(A8), .B(B8), .C_IN(fulladder_8_c_out), .Sum(SUM[8]), .C_OUT(fulladder_9_c_out));
  fullAdder fulladder_10 (.A(A9), .B(B9), .C_IN(fulladder_9_c_out), .Sum(SUM[9]), .C_OUT(fulladder_10_c_out));
  fullAdder fulladder_11 (.A(A10), .B(B10), .C_IN(fulladder_10_c_out), .Sum(SUM[10]), .C_OUT(fulladder_11_c_out));
  fullAdder fulladder_12 (.A(A11), .B(B11), .C_IN(fulladder_11_c_out), .Sum(SUM[11]), .C_OUT(fulladder_12_c_out));
  fullAdder fulladder_13 (.A(A12), .B(B12), .C_IN(fulladder_12_c_out), .Sum(SUM[12]), .C_OUT(fulladder_13_c_out));
  fullAdder fulladder_14 (.A(A13), .B(B13), .C_IN(fulladder_13_c_out), .Sum(SUM[13]), .C_OUT(fulladder_14_c_out));
  fullAdder fulladder_15 (.A(A14), .B(B14), .C_IN(fulladder_14_c_out), .Sum(SUM[14]), .C_OUT(fulladder_15_c_out));
  fullAdder fulladder_16 (.A(A15), .B(B15), .C_IN(fulladder_15_c_out), .Sum(SUM[15]), .C_OUT(fulladder_16_c_out));
  fullAdder fulladder_17 (.A(A16), .B(B16), .C_IN(fulladder_16_c_out), .Sum(SUM[16]), .C_OUT(fulladder_17_c_out));
  fullAdder fulladder_18 (.A(A17), .B(B17), .C_IN(fulladder_17_c_out), .Sum(SUM[17]), .C_OUT(fulladder_18_c_out));
  fullAdder fulladder_19 (.A(A18), .B(B18), .C_IN(fulladder_18_c_out), .Sum(SUM[18]), .C_OUT(fulladder_19_c_out));
  fullAdder fulladder_20 (.A(A19), .B(B19), .C_IN(fulladder_19_c_out), .Sum(SUM[19]), .C_OUT(fulladder_20_c_out));
  fullAdder fulladder_21 (.A(A20), .B(B20), .C_IN(fulladder_20_c_out), .Sum(SUM[20]), .C_OUT(fulladder_21_c_out));
  fullAdder fulladder_22 (.A(A21), .B(B21), .C_IN(fulladder_21_c_out), .Sum(SUM[21]), .C_OUT(fulladder_22_c_out));
  fullAdder fulladder_23 (.A(A22), .B(B22), .C_IN(fulladder_22_c_out), .Sum(SUM[22]), .C_OUT(fulladder_23_c_out));
  fullAdder fulladder_24 (.A(A23), .B(B23), .C_IN(fulladder_23_c_out), .Sum(SUM[23]), .C_OUT(fulladder_24_c_out));
  fullAdder fulladder_25 (.A(A24), .B(B24), .C_IN(fulladder_24_c_out), .Sum(SUM[24]), .C_OUT(fulladder_25_c_out));
  fullAdder fulladder_26 (.A(A25), .B(B25), .C_IN(fulladder_25_c_out), .Sum(SUM[25]), .C_OUT(fulladder_26_c_out));
  fullAdder fulladder_27 (.A(A26), .B(B26), .C_IN(fulladder_26_c_out), .Sum(SUM[26]), .C_OUT(fulladder_27_c_out));
  fullAdder fulladder_28 (.A(A27), .B(B27), .C_IN(fulladder_27_c_out), .Sum(SUM[27]), .C_OUT(fulladder_28_c_out));
  fullAdder fulladder_29 (.A(A28), .B(B28), .C_IN(fulladder_28_c_out), .Sum(SUM[28]), .C_OUT(fulladder_29_c_out));
  fullAdder fulladder_30 (.A(A29), .B(B29), .C_IN(fulladder_29_c_out), .Sum(SUM[29]), .C_OUT(fulladder_30_c_out));
  fullAdder fulladder_31 (.A(A30), .B(B30), .C_IN(fulladder_30_c_out), .Sum(SUM[30]), .C_OUT(fulladder_31_c_out));
  fullAdder fulladder_32 (.A(A31), .B(B31), .C_IN(fulladder_31_c_out), .Sum(SUM[31]), .C_OUT(C_OUT));
  xor xor_1 (Overflow, fulladder_31_c_out, C_OUT);
endmodule

module Shift (
  input  [31:0] bitsIn,
  input  [1:0] shiftOp,
  input  [4:0] shiftAmount,
  output [31:0] bitsOut
);

  wire [0:0] multiplexer_4_out;
  wire [30:0] multiplexer_5_out;
  wire [61:0] multiplexer_4_out_2;
  wire [62:0] extender_1_extended, multiplexer_1_out, multiplexer_2_out, multiplexer_3_out;

  Extender extender_1 (.bitsIn(bitsIn), .shiftOp(shiftOp), .extended(extender_1_extended));
  Multiplexer #(.width(63)) multiplexer_1 (
    .in0(extender_1_extended), .in1({{16{1'b0}}, extender_1_extended[62:16]}), .out(multiplexer_1_out),
    .sel(shiftAmount[4]));
  Multiplexer #(.width(63)) multiplexer_2 (
    .in0(multiplexer_1_out), .in1({{8{1'b0}}, multiplexer_1_out[62:8]}), .out(multiplexer_2_out),
    .sel(shiftAmount[3]));
  Multiplexer #(.width(63)) multiplexer_3 (
    .in0(multiplexer_2_out), .in1({4'b0000, multiplexer_2_out[62:4]}), .out(multiplexer_3_out),
    .sel(shiftAmount[2]));
  Multiplexer #(.width(63)) multiplexer_4 (
    .in0(multiplexer_3_out), .in1({2'b00, multiplexer_3_out[62:2]}),
    .out({multiplexer_4_out_2, multiplexer_4_out[0]}), .sel(shiftAmount[1]));
  Multiplexer #(.width(63)) multiplexer_5 (
    .in0({multiplexer_4_out_2, multiplexer_4_out[0]}), .in1({1'b0, multiplexer_4_out_2}),
    .out({bitsOut, multiplexer_5_out}), .sel(shiftAmount[0]));

  // Notes on the sheet:
  //   00 -> Shift Right Logical
  //   01 -> Shift Right Arithmetic
  //   10 -> Rotate Right
  //   11 -> Shift Left Logical
endmodule

module Arithmetic (
  input  [1:0] ADD_SUB,
  input  [31:0] B,
  input  [31:0] A,
  output [31:0] SUM,
  output Overflow,
  output C_OUT
);

  wire B0, B1, B2, B3, B4, B5, B6, B7, B8, B9, B10, B11, B12, B13, B14, B15, B16, B17, B18, B19, B20, B21,
       B22, B23, B24, B25, B26, B27, B28, B29, B30, B31;
  wire [31:0] bit_extender_1_out;

  assign bit_extender_1_out = {{31{ADD_SUB[0]}}, ADD_SUB[0]};  // Bit_Extender bit_extender_1
  assign {B31, B30, B29, B28, B27, B26, B25, B24, B23, B22, B21, B20, B19, B18, B17, B16, B15, B14, B13, B12, B11, B10, B9, B8, B7, B6, B5, B4, B3, B2, B1, B0} = bit_extender_1_out ^ B;  // XOR_Gate xor_1, 32 bits wide
  rippleCarry ripplecarry_1 (
    .A0(A[0]), .B0(B0), .C_IN(ADD_SUB[0]), .A1(A[1]), .B1(B1), .A2(A[2]), .B2(B2), .A3(A[3]), .B3(B3),
    .A4(A[4]), .B4(B4), .A5(A[5]), .B5(B5), .A6(A[6]), .B6(B6), .A7(A[7]), .B7(B7), .A8(A[8]), .B8(B8),
    .A9(A[9]), .B9(B9), .A10(A[10]), .B10(B10), .A11(A[11]), .B11(B11), .A12(A[12]), .B12(B12), .A13(A[13]),
    .B13(B13), .A14(A[14]), .B14(B14), .A15(A[15]), .B15(B15), .A16(A[16]), .B16(B16), .A17(A[17]),
    .B17(B17), .A18(A[18]), .B18(B18), .A19(A[19]), .B19(B19), .A20(A[20]), .B20(B20), .A21(A[21]),
    .B21(B21), .A22(A[22]), .B22(B22), .A23(A[23]), .B23(B23), .A24(A[24]), .B24(B24), .A25(A[25]),
    .B25(B25), .A26(A[26]), .B26(B26), .A27(A[27]), .B27(B27), .A28(A[28]), .B28(B28), .A29(A[29]),
    .B29(B29), .A30(A[30]), .B30(B30), .A31(A[31]), .B31(B31), .SUM(SUM), .Overflow(Overflow), .C_OUT(C_OUT));

  // Other names for the same wires on the sheet: C_IN = ADD_SUB[0]
endmodule

module ALU (
  input  [31:0] A,
  input  [31:0] B,
  input  [3:0] ALU_SEL,
  output Compare_Out,
  output [31:0] Result,
  output Zero_Flag,
  output Overflow,
  output Arithmetic_Out
);

  wire compare_1_comp;
  wire [31:0] arithmetic_1_sum, bit_extender_1_out, logical_1_result, shift_1_bitsout;

  Shift shift_1 (.bitsIn(A), .shiftOp(ALU_SEL[1:0]), .shiftAmount(B[4:0]), .bitsOut(shift_1_bitsout));
  Compare compare_1 (.SEL(ALU_SEL[1:0]), .B(B), .A(A), .C_OUT(Compare_Out), .COMP(compare_1_comp));
  Arithmetic arithmetic_1 (
    .ADD_SUB(ALU_SEL[1:0]), .B(B), .A(A), .SUM(arithmetic_1_sum), .Overflow(Overflow), .C_OUT(Arithmetic_Out));
  Logical logical_1 (.A(A), .SEL(ALU_SEL[1:0]), .B(B), .Result(logical_1_result));
  assign bit_extender_1_out = {{31{1'b0}}, compare_1_comp};  // Bit_Extender bit_extender_1
  Multiplexer #(.select(2), .width(32)) multiplexer_1 (
    .in0(shift_1_bitsout), .in1(bit_extender_1_out), .in2(arithmetic_1_sum), .in3(logical_1_result),
    .out(Result), .sel(ALU_SEL[3:2]));
  Comparator #(.width(32)) comparator_1 (.a(Result), .b({32{1'b0}}), .eq(Zero_Flag));  // open: gt, lt

  // Other names for the same wires on the sheet: Operation_Bits[1:0] = ALU_SEL[1:0]; Control_Bits[1:0] = ALU_SEL[3:2]
endmodule
